// Logisim project adder subtractor.circ as structural Verilog: 1 circuit, main circuit main
module main (
  input  b0,
  input  b1,
  input  a0,
  input  a1,
  input  a_sign,
  input  b_sign,
  input  switch_mode__add___0__sub___1,
  output r1,
  output r0,
  output r2,
  output end_sign
);

  wire adder_1_cout, adder_2_cout, and_1_out, and_2_out, and_3_out, and_4_out, nand_1_out, nand_2_out,
       nor_1_out, nor_2_out, nor_3_out, not_1_out, not_2_out, xnor_1_out, xor_1_out, xor_2_out, xor_3_out,
       xor_4_out, xor_5_out, xor_6_out, xor_7_out, xor_8_out, xor_9_out, xor_10_out;

  xor xor_1 (xor_1_out, b0, a0);
  xnor xnor_1 (xnor_1_out, b1, a1);
  nor nor_1 (nor_1_out, b1, xnor_1_out);
  nand nand_1 (nand_1_out, b0, xor_1_out);
  nand nand_2 (nand_2_out, xnor_1_out, nand_1_out);
  xor xor_2 (xor_2_out, nor_1_out, nand_2_out);
  nor nor_2 (nor_2_out, nand_2_out, xor_1_out);
  and and_1 (and_1_out, xor_2_out, xor_10_out);
  xor xor_3 (xor_3_out, and_1_out, xor_4_out);
  nor nor_3 (nor_3_out, xor_2_out, nor_2_out);
  xor xor_4 (xor_4_out, xor_10_out, b0);
  xor xor_5 (xor_5_out, and_1_out, a0);
  not not_1 (not_1_out, xor_8_out);
  not not_2 (not_2_out, a_sign);
  and and_2 (and_2_out, nor_3_out, a_sign, not_1_out);
  and and_3 (and_3_out, xor_2_out, not_2_out, xor_8_out);
  or or_1 (end_sign, and_2_out, and_3_out, and_4_out);
  Adder #(.width(1)) adder_1 (.a(xor_5_out), .b(xor_3_out), .out(r0), .cin(xor_10_out), .cout(adder_1_cout));
  xor xor_6 (xor_6_out, xor_10_out, b1);
  xor xor_7 (xor_7_out, and_1_out, xor_6_out);
  xor xor_8 (xor_8_out, b_sign, switch_mode__add___0__sub___1);
  xor xor_9 (xor_9_out, and_1_out, a1);
  Adder #(.width(1)) adder_2 (.a(xor_9_out), .b(xor_7_out), .out(r1), .cin(adder_1_cout), .cout(adder_2_cout));
  xor xor_10 (xor_10_out, a_sign, xor_8_out);
  and and_4 (and_4_out, a_sign, xor_8_out);
  xor xor_11 (r2, adder_2_cout, xor_10_out);

  // Notes on the sheet:
  //   b1
  //   b0
  //   a1
  //   a0
  //   comparator
  //   A=B
  //   A<B
  //   A>B
  //   1 = negative
  //   0 = positive
  //   asign
  //   bsign
  //   a1 a0
  //   b1 b0
  //   _________
  //   sign r2 r1 r0
endmodule
